# Fritzing sketch KOJR (saved by Fritzing 0.9.4)
breadboards: 1

parts:
  Composant1 = Arduino Uno (Rev3) - ICSP
  R1 = Resistor [tolerance=±5% resistance=220 package=THT]
  D1 = Diode [package=diode-1n4001]
  Q1 = pnp-Powertransistor [package="TO220 [THT]"]
  L1 = Solenoid

nets:
  N1: Composant1.D9_PWM, R1.Pin_0
  N2: Composant1.5V, D1.C, L1.pin2
  N3: Composant1.GND, Q1.emitter
  N4: R1.Pin_1, Q1.base
  N5: Q1.collector, L1.pin1
